# Fritzing sketch temperature-display (saved by Fritzing 0.9.3b)
circuit board: 8.46667cm x 5.64444cm
breadboards: 1

parts:
  VCC = female pin header, 6 pins [form="♀ (female)"]
  GND = female pin header, 6 pins [form="♀ (female)"]
  SDA = female pin header, 6 pins [form="♀ (female)"]
  SCL = female pin header, 6 pins [form="♀ (female)"]
  Part3 = Arduino Uno (Rev3)
  T1 = female pin header, 3 pins [form="♀ (female)"]
  T2 = female pin header, 3 pins [form="♀ (female)"]
  T3 = female pin header, 3 pins [form="♀ (female)"]
  R1 = Resistor [tolerance=±5% resistance=4.7k package=THT]

nets:
  N1: VCC.pin1, VCC.pin2, VCC.pin3, VCC.pin4, VCC.pin5, VCC.pin6, Part3.5V, T1.pin3, T2.pin3, T3.pin3, R1.Pin_0
  N2: GND.pin1, GND.pin2, GND.pin3, GND.pin4, GND.pin5, GND.pin6, Part3.GND, T1.pin1, T2.pin1, T3.pin1
  N3: SDA.pin1, SDA.pin2, SDA.pin3, SDA.pin4, SDA.pin5, SDA.pin6, Part3.A4/SDA
  N4: SCL.pin1, SCL.pin2, SCL.pin3, SCL.pin4, SCL.pin5, SCL.pin6, Part3.A5/SCL
  N5: Part3.D2, T1.pin2, T2.pin2, T3.pin2, R1.Pin_1
